// Logisim project ALU.circ as structural Verilog
module half_adder (
  input  X,
  input  Y,
  output SUM,
  output CARRY
);

  xor xor_1 (SUM, X, Y);
  and and_1 (CARRY, X, Y);
endmodule

module full_adder (
  input  CIN,
  input  X,
  input  Y,
  output SUM,
  output COUT
);

  wire half_adder_1_carry, half_adder_1_sum, half_adder_2_carry;

  half_adder half_adder_1 (.X(CIN), .Y(X), .SUM(half_adder_1_sum), .CARRY(half_adder_1_carry));
  half_adder half_adder_2 (.X(half_adder_1_sum), .Y(Y), .SUM(SUM), .CARRY(half_adder_2_carry));
  or or_1 (COUT, half_adder_1_carry, half_adder_2_carry);
endmodule

module nible_adder (
  input  CIN,
  input  X0,
  input  X1,
  input  X2,
  input  X3,
  input  Y0,
  input  Y1,
  input  Y2,
  input  Y3,
  output A0,
  output A1,
  output A2,
  output A3,
  output COUT
);

  wire full_adder_1_cout, full_adder_2_cout, full_adder_3_cout;

  full_adder full_adder_1 (.CIN(CIN), .X(X0), .Y(Y0), .SUM(A0), .COUT(full_adder_1_cout));
  full_adder full_adder_2 (.CIN(full_adder_1_cout), .X(X1), .Y(Y1), .SUM(A1), .COUT(full_adder_2_cout));
  full_adder full_adder_3 (.CIN(full_adder_2_cout), .X(X2), .Y(Y2), .SUM(A2), .COUT(full_adder_3_cout));
  full_adder full_adder_4 (.CIN(full_adder_3_cout), .X(X3), .Y(Y3), .SUM(A3), .COUT(COUT));
endmodule

module nible_invertor (
  input  INV,
  input  X0,
  input  X1,
  input  X2,
  input  X3,
  output O0,
  output O1,
  output O2,
  output O3
);

  xor xor_1 (O0, X0, INV);
  xor xor_2 (O1, X1, INV);
  xor xor_3 (O2, X2, INV);
  xor xor_4 (O3, X3, INV);
endmodule

module nible_arithm (
  input  SUB,
  input  X0,
  input  X1,
  input  X2,
  input  X3,
  input  Y0,
  input  Y1,
  input  Y2,
  input  Y3,
  output A0,
  output A1,
  output A2,
  output A3,
  output CARRY
);

  wire nible_adder_1_cout, nible_invertor_1_o0, nible_invertor_1_o1, nible_invertor_1_o2, nible_invertor_1_o3;

  Hex_Digit_Display hex_digit_display_1 (.value({X3, X2, X1, X0}));  // open: dp
  Hex_Digit_Display hex_digit_display_2 (.value({Y3, Y2, Y1, Y0}));  // open: dp
  Hex_Digit_Display hex_digit_display_3 (.value({3'b000, CARRY}));  // open: dp
  Hex_Digit_Display hex_digit_display_4 (.value({A3, A2, A1, A0}));  // open: dp
  nible_invertor nible_invertor_1 (
    .INV(SUB), .X0(Y0), .X1(Y1), .X2(Y2), .X3(Y3), .O0(nible_invertor_1_o0), .O1(nible_invertor_1_o1),
    .O2(nible_invertor_1_o2), .O3(nible_invertor_1_o3));
  nible_adder nible_adder_1 (
    .CIN(SUB), .X0(X0), .X1(X1), .X2(X2), .X3(X3), .Y0(nible_invertor_1_o0), .Y1(nible_invertor_1_o1),
    .Y2(nible_invertor_1_o2), .Y3(nible_invertor_1_o3), .A0(A0), .A1(A1), .A2(A2), .A3(A3),
    .COUT(nible_adder_1_cout));
  xor xor_1 (CARRY, nible_adder_1_cout, SUB);

  // Notes on the sheet:
  //   +/-
  //   =
endmodule
