// Logisim project dekoder.circ as structural Verilog: 1 circuit, main circuit main
module main (
  input  A,
  input  B,
  input  C,
  input  D,
  output nA,
  output nB,
  output nC,
  output nD,
  output Y
);

  wire nand_1_out, nand_2_out, nand_3_out;

  not not_1 (nD, D);
  not not_2 (nC, C);
  not not_3 (nB, B);
  not not_4 (nA, A);
  nand nand_1 (nand_1_out, nD, nC);
  nand nand_2 (nand_2_out, B, nD);
  nand nand_3 (nand_3_out, B, nC);
  nand nand_4 (Y, nA, nand_1_out, nand_2_out, nand_3_out);

  // Notes on the sheet:
  //   Zde jsou negace,
  //   negace B se nepoužívá
  //   nA
  //   nC . nD
  //   B . nD
  //   B . nC
endmodule
