// Logisim project AdderDecMux.circ as structural Verilog
module half_adder (
  input  X,
  input  Y,
  output SUM,
  output CARRY
);

  xor xor_1 (SUM, X, Y);
  and and_1 (CARRY, X, Y);
endmodule

module full_adder (
  input  CIN,
  input  X,
  input  Y,
  output SUM,
  output COUT
);

  wire half_adder_1_carry, half_adder_1_sum, half_adder_2_carry;

  half_adder half_adder_1 (.X(CIN), .Y(X), .SUM(half_adder_1_sum), .CARRY(half_adder_1_carry));
  half_adder half_adder_2 (.X(half_adder_1_sum), .Y(Y), .SUM(SUM), .CARRY(half_adder_2_carry));
  or or_1 (COUT, half_adder_1_carry, half_adder_2_carry);
endmodule

module nible_adder (
  input  CIN,
  input  X0,
  input  X1,
  input  X2,
  input  X3,
  input  Y0,
  input  Y1,
  input  Y2,
  input  Y3,
  output A0,
  output A1,
  output A2,
  output A3,
  output COUT
);

  wire full_adder_1_cout, full_adder_2_cout, full_adder_3_cout;

  full_adder full_adder_1 (.CIN(CIN), .X(X0), .Y(Y0), .SUM(A0), .COUT(full_adder_1_cout));
  full_adder full_adder_2 (.CIN(full_adder_1_cout), .X(X1), .Y(Y1), .SUM(A1), .COUT(full_adder_2_cout));
  full_adder full_adder_3 (.CIN(full_adder_2_cout), .X(X2), .Y(Y2), .SUM(A2), .COUT(full_adder_3_cout));
  full_adder full_adder_4 (.CIN(full_adder_3_cout), .X(X3), .Y(Y3), .SUM(A3), .COUT(COUT));
endmodule

module nible_invertor (
  input  INV,
  input  X0,
  input  X1,
  input  X2,
  input  X3,
  output O0,
  output O1,
  output O2,
  output O3
);

  xor xor_1 (O0, X0, INV);
  xor xor_2 (O1, X1, INV);
  xor xor_3 (O2, X2, INV);
  xor xor_4 (O3, X3, INV);
endmodule

module nible_arithm (
  input  SUB,
  input  X0,
  input  X1,
  input  X2,
  input  X3,
  input  Y0,
  input  Y1,
  input  Y2,
  input  Y3,
  output A0,
  output A1,
  output A2,
  output A3,
  output CARRY
);

  wire nible_adder_1_cout, nible_invertor_1_o0, nible_invertor_1_o1, nible_invertor_1_o2, nible_invertor_1_o3;

  Hex_Digit_Display hex_digit_display_1 (.value({X3, X2, X1, X0}));  // open: dp
  Hex_Digit_Display hex_digit_display_2 (.value({Y3, Y2, Y1, Y0}));  // open: dp
  Hex_Digit_Display hex_digit_display_3 (.value({3'b000, CARRY}));  // open: dp
  Hex_Digit_Display hex_digit_display_4 (.value({A3, A2, A1, A0}));  // open: dp
  nible_invertor nible_invertor_1 (
    .INV(SUB), .X0(Y0), .X1(Y1), .X2(Y2), .X3(Y3), .O0(nible_invertor_1_o0), .O1(nible_invertor_1_o1),
    .O2(nible_invertor_1_o2), .O3(nible_invertor_1_o3));
  nible_adder nible_adder_1 (
    .CIN(SUB), .X0(X0), .X1(X1), .X2(X2), .X3(X3), .Y0(nible_invertor_1_o0), .Y1(nible_invertor_1_o1),
    .Y2(nible_invertor_1_o2), .Y3(nible_invertor_1_o3), .A0(A0), .A1(A1), .A2(A2), .A3(A3),
    .COUT(nible_adder_1_cout));
  xor xor_1 (CARRY, nible_adder_1_cout, SUB);

  // Notes on the sheet:
  //   +/-
  //   =
endmodule

module decoder_1_of_8 (
  input  A0,
  input  A1,
  input  A2,
  output Y0,
  output Y1,
  output Y2,
  output Y3,
  output Y4,
  output Y5,
  output Y6,
  output Y7
);

  wire not_1_out, not_2_out, not_3_out;

  not not_1 (not_1_out, A0);
  not not_2 (not_2_out, A1);
  not not_3 (not_3_out, A2);
  and and_1 (Y0, not_1_out, not_2_out, not_3_out);
  and and_2 (Y1, A0, not_2_out, not_3_out);
  and and_3 (Y2, not_1_out, A1, not_3_out);
  and and_4 (Y3, A0, A1, not_3_out);
  and and_5 (Y4, not_1_out, not_2_out, A2);
  and and_6 (Y5, A0, not_2_out, A2);
  and and_7 (Y6, not_1_out, A1, A2);
  and and_8 (Y7, A0, A1, A2);
endmodule

module mux_8 (
  input  X0,
  input  X1,
  input  X2,
  input  X3,
  input  X4,
  input  X5,
  input  X6,
  input  X7,
  input  A0,
  input  A1,
  input  A2,
  output Y
);

  wire and_1_out, and_2_out, and_3_out, and_4_out, and_5_out, and_6_out, and_7_out, and_8_out,
       decoder_1_of_8_1_y0, decoder_1_of_8_1_y1, decoder_1_of_8_1_y2, decoder_1_of_8_1_y3,
       decoder_1_of_8_1_y4, decoder_1_of_8_1_y5, decoder_1_of_8_1_y6, decoder_1_of_8_1_y7;

  decoder_1_of_8 decoder_1_of_8_1 (
    .A0(A0), .A1(A1), .A2(A2), .Y0(decoder_1_of_8_1_y0), .Y1(decoder_1_of_8_1_y1), .Y2(decoder_1_of_8_1_y2),
    .Y3(decoder_1_of_8_1_y3), .Y4(decoder_1_of_8_1_y4), .Y5(decoder_1_of_8_1_y5), .Y6(decoder_1_of_8_1_y6),
    .Y7(decoder_1_of_8_1_y7));
  and and_1 (and_1_out, X0, decoder_1_of_8_1_y0);
  and and_2 (and_2_out, X1, decoder_1_of_8_1_y1);
  and and_3 (and_3_out, X2, decoder_1_of_8_1_y2);
  and and_4 (and_4_out, X3, decoder_1_of_8_1_y3);
  and and_5 (and_5_out, X4, decoder_1_of_8_1_y4);
  and and_6 (and_6_out, X5, decoder_1_of_8_1_y5);
  and and_7 (and_7_out, X6, decoder_1_of_8_1_y6);
  and and_8 (and_8_out, X7, decoder_1_of_8_1_y7);
  or or_1 (Y, and_1_out, and_2_out, and_3_out, and_4_out, and_5_out, and_6_out, and_7_out, and_8_out);
endmodule

module demux_8 (
  input  X,
  input  A0,
  input  A1,
  input  A2,
  output Y0,
  output Y1,
  output Y2,
  output Y3,
  output Y4,
  output Y5,
  output Y6,
  output Y7
);

  wire decoder_1_of_8_1_y0, decoder_1_of_8_1_y1, decoder_1_of_8_1_y2, decoder_1_of_8_1_y3,
       decoder_1_of_8_1_y4, decoder_1_of_8_1_y5, decoder_1_of_8_1_y6, decoder_1_of_8_1_y7;

  decoder_1_of_8 decoder_1_of_8_1 (
    .A0(A0), .A1(A1), .A2(A2), .Y0(decoder_1_of_8_1_y0), .Y1(decoder_1_of_8_1_y1), .Y2(decoder_1_of_8_1_y2),
    .Y3(decoder_1_of_8_1_y3), .Y4(decoder_1_of_8_1_y4), .Y5(decoder_1_of_8_1_y5), .Y6(decoder_1_of_8_1_y6),
    .Y7(decoder_1_of_8_1_y7));
  and and_1 (Y0, X, decoder_1_of_8_1_y0);
  and and_2 (Y1, X, decoder_1_of_8_1_y1);
  and and_3 (Y2, X, decoder_1_of_8_1_y2);
  and and_4 (Y3, X, decoder_1_of_8_1_y3);
  and and_5 (Y4, X, decoder_1_of_8_1_y4);
  and and_6 (Y5, X, decoder_1_of_8_1_y5);
  and and_7 (Y6, X, decoder_1_of_8_1_y6);
  and and_8 (Y7, X, decoder_1_of_8_1_y7);
endmodule

module Symboly (
);

  wire decoder_1_out0, decoder_1_out1, decoder_1_out2, decoder_1_out3, decoder_1_out4, decoder_1_out5,
       decoder_1_out6, decoder_1_out7, demultiplexer_1_out0, demultiplexer_1_out1, demultiplexer_1_out2,
       demultiplexer_1_out3, demultiplexer_1_out4, demultiplexer_1_out5, demultiplexer_1_out6,
       demultiplexer_1_out7, multiplexer_1_out, undriven, undriven_2, undriven_3, undriven_4, undriven_5,
       undriven_6, undriven_7, undriven_8, undriven_9;

  Multiplexer #(.select(3)) multiplexer_1 (
    .in0(undriven), .in1(undriven_2), .in2(undriven_3), .in3(undriven_4), .in4(undriven_5), .in5(undriven_6),
    .in6(undriven_7), .in7(undriven_8), .out(multiplexer_1_out));  // open: sel
  Demultiplexer #(.select(3)) demultiplexer_1 (
    .out0(demultiplexer_1_out0), .out1(demultiplexer_1_out1), .out2(demultiplexer_1_out2),
    .out3(demultiplexer_1_out3), .out4(demultiplexer_1_out4), .out5(demultiplexer_1_out5),
    .out6(demultiplexer_1_out6), .out7(demultiplexer_1_out7), .in(undriven_9));  // open: sel
  Decoder #(.select(3)) decoder_1 (
    .out0(decoder_1_out0), .out1(decoder_1_out1), .out2(decoder_1_out2), .out3(decoder_1_out3),
    .out4(decoder_1_out4), .out5(decoder_1_out5), .out6(decoder_1_out6), .out7(decoder_1_out7));  // open: sel, en

  // Notes on the sheet:
  //   X
  //   SUM
  //   Y
  //   CIN
  //   C
  //   1
  //   3
  //   2
  //   4
endmodule
