// Logisim project FlipFlops.circ as structural Verilog
module RS_KO (
  input  S,
  input  R,
  output Q
);

  wire nand_1_out, nand_2_out, nand_4_out;

  nand nand_1 (nand_1_out, S, S);
  nand nand_2 (nand_2_out, R, R);
  nand nand_3 (Q, nand_1_out, nand_4_out);
  nand nand_4 (nand_4_out, Q, nand_2_out);
endmodule

module RST_KO (
  input  S,
  input  T,
  input  R,
  output Q,
  output nQ
);

  wire nand_1_out, nand_2_out;

  nand nand_1 (nand_1_out, S, T);
  nand nand_2 (nand_2_out, T, R);
  nand nand_3 (Q, nand_1_out, nQ);
  nand nand_4 (nQ, Q, nand_2_out);
endmodule

module D_KO (
  input  D,
  input  CLK,
  output Q,
  output nQ
);

  wire not_1_out, not_2_out, not_3_out, rst_ko_1_nq, rst_ko_1_q;

  not not_1 (not_1_out, D);
  not not_2 (not_2_out, CLK);
  RST_KO rst_ko_1 (.S(D), .T(not_2_out), .R(not_1_out), .Q(rst_ko_1_q), .nQ(rst_ko_1_nq));
  not not_3 (not_3_out, not_2_out);
  RST_KO rst_ko_2 (.S(rst_ko_1_q), .T(not_3_out), .R(rst_ko_1_nq), .Q(Q), .nQ(nQ));
endmodule

module D_KO_divider (
  output Q0
);

  wire CLK_out, d_ff_1_qn;

  D_Flip_Flop d_ff_1 (.D(d_ff_1_qn), .clk(CLK_out), .Q(Q0), .Qn(d_ff_1_qn));  // open: preset, reset
  Clock CLK (.out(CLK_out));
endmodule

module D_KO_cnt_down (
  output Q0,
  output Q1,
  output Q2,
  output Q3
);

  wire CLK_out, d_ff_1_qn, d_ff_2_qn, d_ff_3_qn, d_ff_4_qn;

  D_Flip_Flop d_ff_1 (.D(d_ff_1_qn), .clk(CLK_out), .Q(Q0), .Qn(d_ff_1_qn));  // open: preset, reset
  Clock CLK (.out(CLK_out));
  D_Flip_Flop d_ff_2 (.D(d_ff_2_qn), .clk(Q0), .Q(Q1), .Qn(d_ff_2_qn));  // open: preset, reset
  D_Flip_Flop d_ff_3 (.D(d_ff_3_qn), .clk(Q1), .Q(Q2), .Qn(d_ff_3_qn));  // open: preset, reset
  D_Flip_Flop d_ff_4 (.D(d_ff_4_qn), .clk(Q2), .Q(Q3), .Qn(d_ff_4_qn));  // open: preset, reset
endmodule

module D_KO_cnt_up (
  output Q0,
  output Q1,
  output Q2,
  output Q3
);

  wire CLK_out, d_ff_1_q, d_ff_2_q, d_ff_3_q;

  D_Flip_Flop d_ff_1 (.D(Q0), .clk(CLK_out), .Q(d_ff_1_q), .Qn(Q0));  // open: preset, reset
  Clock CLK (.out(CLK_out));
  D_Flip_Flop d_ff_2 (.D(Q1), .clk(d_ff_1_q), .Q(d_ff_2_q), .Qn(Q1));  // open: preset, reset
  D_Flip_Flop d_ff_3 (.D(Q2), .clk(d_ff_2_q), .Q(d_ff_3_q), .Qn(Q2));  // open: preset, reset
  D_Flip_Flop d_ff_4 (.D(Q3), .clk(d_ff_3_q), .Qn(Q3));  // open: Q, preset, reset
endmodule

module D_KO_shift (
  output Q0,
  output Q1,
  output Q2,
  output Q3
);

  wire CLK_out, nand_1_out;

  Clock CLK (.out(CLK_out));
  D_Flip_Flop d_ff_1 (.D(nand_1_out), .clk(CLK_out), .Q(Q0));  // open: Qn, preset, reset
  nand nand_1 (nand_1_out, Q0, Q1, Q2, Q3);
  D_Flip_Flop d_ff_2 (.D(Q0), .clk(CLK_out), .Q(Q1));  // open: Qn, preset, reset
  D_Flip_Flop d_ff_3 (.D(Q1), .clk(CLK_out), .Q(Q2));  // open: Qn, preset, reset
  D_Flip_Flop d_ff_4 (.D(Q2), .clk(CLK_out), .Q(Q3));  // open: Qn, preset, reset
endmodule

module D_KO_cnt_sync (
  output Q0,
  output Q1,
  output Q2
);

  wire and_1_out, CLK_out, d_ff_1_qn, xor_1_out, xor_2_out;

  Clock CLK (.out(CLK_out));
  D_Flip_Flop d_ff_1 (.D(d_ff_1_qn), .clk(CLK_out), .Q(Q0), .Qn(d_ff_1_qn));  // open: preset, reset
  xor xor_1 (xor_1_out, Q1, Q0);
  D_Flip_Flop d_ff_2 (.D(xor_1_out), .clk(CLK_out), .Q(Q1));  // open: Qn, preset, reset
  and and_1 (and_1_out, Q0, Q1);
  xor xor_2 (xor_2_out, Q2, and_1_out);
  D_Flip_Flop d_ff_3 (.D(xor_2_out), .clk(CLK_out), .Q(Q2));  // open: Qn, preset, reset
endmodule
