// Logisim project ALU.circ as structural Verilog: 14 circuits, main circuit main
module main (
  input  [3:0] X,
  input  [3:0] Y,
  input  [3:0] CMD,
  output [3:0] O,
  output CARRY,
  output ZERO
);

  nible_alu nible_alu_1 (.X(X), .Y(Y), .CMD(CMD), .O(O), .CARRY(CARRY));
  nor nor_1 (ZERO, O[0], O[1], O[2], O[3]);

  // Notes on the sheet:
  //   Vstupy
  //   CMD
  //   0001
  //   0100
  //   1000
  //   1100
  //   1110
  //   OPERACE
  //   Negace X
  //   X or Y
  //   X and Y
  //   X+Y
  //   X-Y
  //   Poznámka
  //   Bity 0 a 1 určují negaci operandů
  //   Bity 0 a 1 určují negaci operandů
  //   Výstup
  //   Příznaky
endmodule

module half_adder (
  input  X,
  input  Y,
  output SUM,
  output CARRY
);

  xor xor_1 (SUM, X, Y);
  and and_1 (CARRY, X, Y);
endmodule

module full_adder (
  input  CIN,
  input  X,
  input  Y,
  output SUM,
  output COUT
);

  wire half_adder_1_carry, half_adder_1_sum, half_adder_2_carry;

  half_adder half_adder_1 (.X(CIN), .Y(X), .SUM(half_adder_1_sum), .CARRY(half_adder_1_carry));
  half_adder half_adder_2 (.X(half_adder_1_sum), .Y(Y), .SUM(SUM), .CARRY(half_adder_2_carry));
  or or_1 (COUT, half_adder_1_carry, half_adder_2_carry);
endmodule

module nible_adder (
  input  CIN,
  input  [3:0] X,
  input  [3:0] Y,
  output [3:0] O,
  output COUT
);

  wire full_adder_1_cout, full_adder_2_cout, full_adder_3_cout;

  full_adder full_adder_1 (.CIN(CIN), .X(X[0]), .Y(Y[0]), .SUM(O[0]), .COUT(full_adder_1_cout));
  full_adder full_adder_2 (.CIN(full_adder_1_cout), .X(X[1]), .Y(Y[1]), .SUM(O[1]), .COUT(full_adder_2_cout));
  full_adder full_adder_3 (.CIN(full_adder_2_cout), .X(X[2]), .Y(Y[2]), .SUM(O[2]), .COUT(full_adder_3_cout));
  full_adder full_adder_4 (.CIN(full_adder_3_cout), .X(X[3]), .Y(Y[3]), .SUM(O[3]), .COUT(COUT));
endmodule

module nible_invertor (
  input  INV,
  input  X0,
  input  X1,
  input  X2,
  input  X3,
  output O0,
  output O1,
  output O2,
  output O3
);

  xor xor_1 (O0, X0, INV);
  xor xor_2 (O1, X1, INV);
  xor xor_3 (O2, X2, INV);
  xor xor_4 (O3, X3, INV);
endmodule

module decoder_1_of_8 (
  input  A0,
  input  A1,
  input  A2,
  output Y0,
  output Y1,
  output Y2,
  output Y3,
  output Y4,
  output Y5,
  output Y6,
  output Y7
);

  wire not_1_out, not_2_out, not_3_out;

  not not_1 (not_1_out, A0);
  not not_2 (not_2_out, A1);
  not not_3 (not_3_out, A2);
  and and_1 (Y0, not_1_out, not_2_out, not_3_out);
  and and_2 (Y1, A0, not_2_out, not_3_out);
  and and_3 (Y2, not_1_out, A1, not_3_out);
  and and_4 (Y3, A0, A1, not_3_out);
  and and_5 (Y4, not_1_out, not_2_out, A2);
  and and_6 (Y5, A0, not_2_out, A2);
  and and_7 (Y6, not_1_out, A1, A2);
  and and_8 (Y7, A0, A1, A2);
endmodule

module mux_8_bus (
  input  X0,
  input  X1,
  input  X2,
  input  X3,
  input  X4,
  input  X5,
  input  X6,
  input  X7,
  input  A0,
  input  A1,
  input  A2,
  output BUS1BIT
);

  wire decoder_1_of_8_1_y0, decoder_1_of_8_1_y1, decoder_1_of_8_1_y2, decoder_1_of_8_1_y3,
       decoder_1_of_8_1_y4, decoder_1_of_8_1_y5, decoder_1_of_8_1_y6, decoder_1_of_8_1_y7;

  assign BUS1BIT = decoder_1_of_8_1_y0 ? X0 : 1'bz;  // Controlled_Buffer controlled_buffer_1
  decoder_1_of_8 decoder_1_of_8_1 (
    .A0(A0), .A1(A1), .A2(A2), .Y0(decoder_1_of_8_1_y0), .Y1(decoder_1_of_8_1_y1), .Y2(decoder_1_of_8_1_y2),
    .Y3(decoder_1_of_8_1_y3), .Y4(decoder_1_of_8_1_y4), .Y5(decoder_1_of_8_1_y5), .Y6(decoder_1_of_8_1_y6),
    .Y7(decoder_1_of_8_1_y7));
  assign BUS1BIT = decoder_1_of_8_1_y1 ? X1 : 1'bz;  // Controlled_Buffer controlled_buffer_2
  assign BUS1BIT = decoder_1_of_8_1_y2 ? X2 : 1'bz;  // Controlled_Buffer controlled_buffer_3
  assign BUS1BIT = decoder_1_of_8_1_y3 ? X3 : 1'bz;  // Controlled_Buffer controlled_buffer_4
  assign BUS1BIT = decoder_1_of_8_1_y4 ? X4 : 1'bz;  // Controlled_Buffer controlled_buffer_5
  assign BUS1BIT = decoder_1_of_8_1_y5 ? X5 : 1'bz;  // Controlled_Buffer controlled_buffer_6
  assign BUS1BIT = decoder_1_of_8_1_y6 ? X6 : 1'bz;  // Controlled_Buffer controlled_buffer_7
  assign BUS1BIT = decoder_1_of_8_1_y7 ? X7 : 1'bz;  // Controlled_Buffer controlled_buffer_8

  // Notes on the sheet:
  //   Sdílený vodič
endmodule

module nible_or (
  input  [3:0] X,
  input  [3:0] Y,
  output [3:0] O
);

  or or_1 (O[0], X[0], Y[0]);
  or or_2 (O[1], Y[1], X[1]);
  or or_3 (O[2], Y[2], X[2]);
  or or_4 (O[3], Y[3], X[3]);
endmodule

module nible_and (
  input  [3:0] X,
  input  [3:0] Y,
  output [3:0] O
);

  and and_1 (O[0], X[0], Y[0]);
  and and_2 (O[1], Y[1], X[1]);
  and and_3 (O[2], Y[2], X[2]);
  and and_4 (O[3], Y[3], X[3]);
endmodule

module nible_inv (
  input  [3:0] X,
  input  INV,
  output [3:0] O
);

  xor xor_1 (O[0], X[0], INV);
  xor xor_2 (O[1], INV, X[1]);
  xor xor_3 (O[2], INV, X[2]);
  xor xor_4 (O[3], INV, X[3]);
endmodule

module nible_alu (
  input  [3:0] X,
  input  [3:0] Y,
  input  [3:0] CMD,
  output [3:0] O,
  output CARRY
);

  wire nible_adder_1_cout, xor_1_out;
  wire [3:0] nible_adder_1_o, nible_and_1_o, nible_inv_1_o, nible_inv_2_o, nible_or_1_o;

  nible_inv nible_inv_1 (.X(X), .INV(CMD[0]), .O(nible_inv_1_o));
  nible_inv nible_inv_2 (.X(Y), .INV(CMD[1]), .O(nible_inv_2_o));
  nible_or nible_or_1 (.X(nible_inv_1_o), .Y(nible_inv_2_o), .O(nible_or_1_o));
  nible_and nible_and_1 (.X(nible_inv_1_o), .Y(nible_inv_2_o), .O(nible_and_1_o));
  nible_adder nible_adder_1 (
    .CIN(CMD[1]), .X(nible_inv_1_o), .Y(nible_inv_2_o), .O(nible_adder_1_o), .COUT(nible_adder_1_cout));
  Multiplexer #(.select(2), .width(4)) multiplexer_1 (
    .in0(nible_inv_1_o), .in1(nible_or_1_o), .in2(nible_and_1_o), .in3(nible_adder_1_o), .out(O),
    .sel(CMD[3:2]));
  xor xor_1 (xor_1_out, nible_adder_1_cout, CMD[1]);
  and and_1 (CARRY, xor_1_out, CMD[2], CMD[3]);
endmodule

module nible_register (
  input  [3:0] X,
  input  WR,
  input  CLK,
  output [3:0] O
);

  wire multiplexer_1_out, multiplexer_2_out, multiplexer_3_out, multiplexer_4_out;

  Multiplexer multiplexer_1 (.in0(O[0]), .in1(X[0]), .out(multiplexer_1_out), .sel(WR));
  Multiplexer multiplexer_2 (.in0(O[1]), .in1(X[1]), .out(multiplexer_2_out), .sel(WR));
  Multiplexer multiplexer_3 (.in0(O[2]), .in1(X[2]), .out(multiplexer_3_out), .sel(WR));
  Multiplexer multiplexer_4 (.in0(O[3]), .in1(X[3]), .out(multiplexer_4_out), .sel(WR));
  D_Flip_Flop d_ff_1 (.D(multiplexer_1_out), .clk(CLK), .Q(O[0]));  // open: Qn, preset, reset
  D_Flip_Flop d_ff_2 (.D(multiplexer_2_out), .clk(CLK), .Q(O[1]));  // open: Qn, preset, reset
  D_Flip_Flop d_ff_3 (.D(multiplexer_3_out), .clk(CLK), .Q(O[2]));  // open: Qn, preset, reset
  D_Flip_Flop d_ff_4 (.D(multiplexer_4_out), .clk(CLK), .Q(O[3]));  // open: Qn, preset, reset
endmodule

module nible_acumulator (
  input  [3:0] ACUM,
  input  [3:0] X,
  input  WR,
  input  CLK,
  output [3:0] O
);

  wire multiplexer_1_out, multiplexer_2_out, multiplexer_3_out, multiplexer_4_out;

  Multiplexer multiplexer_1 (.in0(ACUM[0]), .in1(X[0]), .out(multiplexer_1_out), .sel(WR));
  Multiplexer multiplexer_2 (.in0(ACUM[1]), .in1(X[1]), .out(multiplexer_2_out), .sel(WR));
  Multiplexer multiplexer_3 (.in0(ACUM[2]), .in1(X[2]), .out(multiplexer_3_out), .sel(WR));
  Multiplexer multiplexer_4 (.in0(ACUM[3]), .in1(X[3]), .out(multiplexer_4_out), .sel(WR));
  D_Flip_Flop d_ff_1 (.D(multiplexer_1_out), .clk(CLK), .Q(O[0]));  // open: Qn, preset, reset
  D_Flip_Flop d_ff_2 (.D(multiplexer_2_out), .clk(CLK), .Q(O[1]));  // open: Qn, preset, reset
  D_Flip_Flop d_ff_3 (.D(multiplexer_3_out), .clk(CLK), .Q(O[2]));  // open: Qn, preset, reset
  D_Flip_Flop d_ff_4 (.D(multiplexer_4_out), .clk(CLK), .Q(O[3]));  // open: Qn, preset, reset
endmodule

module alu_acum (
  input  WR,
  input  CLK,
  input  [3:0] MEM,
  input  [3:0] CMD,
  output [3:0] ACUM,
  output CARRY,
  output ZERO
);

  wire [3:0] ACC_o;

  nible_acumulator ACC (.ACUM(ACUM), .X(MEM), .WR(WR), .CLK(CLK), .O(ACC_o));
  main ALU (.X(ACC_o), .Y(MEM), .CMD(CMD), .O(ACUM), .CARRY(CARRY), .ZERO(ZERO));

  // Notes on the sheet:
  //   Vstupy
  //   Výstup
endmodule
