// Logisim project hazardy.circ as structural Verilog
module hazard_static_solution (
  input  A,
  input  B,
  input  C,
  output Y
);

  wire and_1_out, and_2_out, and_3_out, not_1_out;

  not not_1 (not_1_out, A);
  and and_1 (and_1_out, A, B);
  and and_2 (and_2_out, not_1_out, C);
  and and_3 (and_3_out, B, C);
  or or_1 (Y, and_1_out, and_2_out, and_3_out);

  // Notes on the sheet:
  //   Trvale 1 při (A, B) =1
endmodule

module hazard_static (
  input  A,
  input  B,
  input  C,
  output Y
);

  wire and_1_out, and_2_out, not_1_out;

  not not_1 (not_1_out, A);
  and and_1 (and_1_out, A, B);
  and and_2 (and_2_out, not_1_out, C);
  or or_1 (Y, and_1_out, and_2_out);

  // Notes on the sheet:
  //   Invertor vytváří zpoždění
  //   Problematický přechod je změna A při současném (B, C) =1
endmodule

module CU_asynch (
  input  CLK,
  output Q_N
);

  wire d_ff_1_qn;

  D_Flip_Flop d_ff_1 (.D(d_ff_1_qn), .clk(CLK), .Q(Q_N), .Qn(d_ff_1_qn));  // open: preset, reset

  // Notes on the sheet:
  //   Q(N-1)
endmodule

module CU_synch (
  input  AND_N_1,
  input  Q_N_1,
  input  CLK,
  output AND_N,
  output Q_N
);

  wire xor_1_out;

  and and_1 (AND_N, AND_N_1, Q_N_1);
  D_Flip_Flop d_ff_1 (.D(xor_1_out), .clk(CLK), .Q(Q_N));  // open: Qn, preset, reset
  xor xor_1 (xor_1_out, Q_N, AND_N);
endmodule

module hazard_static_sync (
  input  A,
  input  B,
  input  C,
  input  CLK,
  output Y
);

  wire and_1_out, and_2_out, not_1_out, or_1_out;

  not not_1 (not_1_out, A);
  and and_1 (and_1_out, A, B);
  and and_2 (and_2_out, not_1_out, C);
  D_Flip_Flop d_ff_1 (.D(or_1_out), .clk(CLK), .Q(Y));  // open: Qn, preset, reset
  or or_1 (or_1_out, and_1_out, and_2_out);
endmodule
